# Fritzing sketch Ritto_McuV3_Doorbell (saved by Fritzing 0.9.5d)
circuit board: 8.46667cm x 5.64444cm
breadboards: 1

parts:
  U3 = Optocoupler [package=THT]
  R1 = Resistor [tolerance=±5% resistance=220 package=THT]
  R2 = Resistor [tolerance=±5% resistance=220 package=THT]
  RITTO_PCB = male pin header, 4 pins [form="♂ (male)"]
  U2 = Optocoupler [package=THT]
  U4 = Optocoupler [package=THT]
  R3 = Resistor [tolerance=±5% resistance=1k package=THT]
  U1 = NodeMCU V3.0

nets:
  N1: U3.Pin_1, R2.Pin_0
  NODEMCU_GND: U3.Pin_2, U2.Pin_2, U4.Pin_4, U1.GND
  RITTO_GND: U3.Pin_4, RITTO_PCB.pin1, U2.Pin_4, U4.Pin_2
  N2: U3.Pin_5, RITTO_PCB.pin3
  N3: R1.Pin_0, U2.Pin_1
  N4: R1.Pin_1, U1.D2
  N5: R2.Pin_1, U1.D1
  N6: RITTO_PCB.pin2, U2.Pin_5
  N7: RITTO_PCB.pin4, R3.Pin_0
  N8: U4.Pin_1, R3.Pin_1
  N9: U4.Pin_5, U1.D5

notes:
  GND
  LAUT
  TÖ
  EXT
  RITTO_PCB
  Pin 1: GND
  Pin 2: LAUT
  Pin 3: TÖ
  Pin 4: EXT (Klingel-Puls 5V)
  Ritto Smart Doorbell, Ritto 7630 Türklingel Smart Home,       1.0

custom parts:
  NodeMCU V3.0: ESP8266 based NodeMCU
